// Logisim project CN262_Project-final.circ as structural Verilog: 8 circuits, main circuit main
module main (
);

  wire a, b, c, clk, EN, jackpot, reset;
  wire [1:0] new_random_1_prize_output;
  wire [3:0] n7_sec_1_out_2, n7_sec_1_out_3, n7_sec_1_out_4, new_random_1_out_3, new_random_1_out_4,
       new_random_1_out_5;
  wire [7:0] adder_1_out, coins_1_output, reward_1_out_4;
  wire [15:0] display_1_out_4, display_1_out_5, display_1_out_6, display_1_out_7, display_1_out_8,
       display_1_out_9, display_1_out_10, display_1_out_11, display_1_out_12, display_1_out_13,
       display_1_out_14, display_1_out_15, display_1_out_16, display_1_out_17, display_1_out_18,
       display_1_out_19, display_2_out_4, display_2_out_5, display_2_out_6, display_2_out_7, display_2_out_8,
       display_2_out_9, display_2_out_10, display_2_out_11, display_2_out_12, display_2_out_13,
       display_2_out_14, display_2_out_16, display_2_out_17, display_2_out_18, display_2_out_19,
       display_3_out_4, display_3_out_5, display_3_out_6, display_3_out_7, display_3_out_8, display_3_out_9,
       display_3_out_10, display_3_out_11, display_3_out_12, display_3_out_13, display_3_out_14,
       display_3_out_15, display_3_out_16, display_3_out_17, display_3_out_18, display_3_out_19;

  Clock clock_1 (.out(clk));
  Button button_1 (.out(EN));
  Button button_2 (.out(reset));
  Display display_1 (
    .select(a), .clk(clk), .in_3(new_random_1_out_3), .out_19(display_1_out_19), .out_18(display_1_out_18),
    .out_17(display_1_out_17), .out_16(display_1_out_16), .out_4(display_1_out_4), .out_5(display_1_out_5),
    .out_6(display_1_out_6), .out_7(display_1_out_7), .out_8(display_1_out_8), .out_9(display_1_out_9),
    .out_10(display_1_out_10), .out_11(display_1_out_11), .out_12(display_1_out_12),
    .out_13(display_1_out_13), .out_14(display_1_out_14), .out_15(display_1_out_15));
  DotMatrix #(.matrixcols(16), .matrixrows(16)) dotmatrix_1 (
    .col0(display_1_out_19), .col1(display_1_out_18), .col2(display_1_out_17), .col3(display_1_out_16),
    .col4(display_1_out_4), .col5(display_1_out_5), .col6(display_1_out_6), .col7(display_1_out_7),
    .col8(display_1_out_8), .col9(display_1_out_9), .col10(display_1_out_10), .col11(display_1_out_11),
    .col12(display_1_out_12), .col13(display_1_out_13), .col14(display_1_out_14), .col15(display_1_out_15));
  new_Random new_random_1 (
    .clock(clk), .button(EN), .Check_win(jackpot), .Prize_output(new_random_1_prize_output), .Select1(a),
    .Select2(c), .Select3(b), .out_3(new_random_1_out_3), .out_4(new_random_1_out_4),
    .out_5(new_random_1_out_5));
  LED led_1 (.in(jackpot));
  DotMatrix #(.matrixcols(16), .matrixrows(16)) dotmatrix_2 (
    .col0(display_2_out_19), .col1(display_2_out_18), .col2(display_2_out_17), .col3(display_2_out_16),
    .col4(display_2_out_4), .col5(display_2_out_5), .col6(display_2_out_6), .col7(display_2_out_7),
    .col8(display_2_out_8), .col9(display_2_out_9), .col10(display_2_out_10), .col11(display_2_out_11),
    .col12(display_2_out_12), .col13(display_2_out_13), .col14(display_2_out_14), .col15(display_2_out_14));
  Display display_2 (
    .select(b), .clk(clk), .in_3(new_random_1_out_4), .out_19(display_2_out_19), .out_18(display_2_out_18),
    .out_17(display_2_out_17), .out_16(display_2_out_16), .out_4(display_2_out_4), .out_5(display_2_out_5),
    .out_6(display_2_out_6), .out_7(display_2_out_7), .out_8(display_2_out_8), .out_9(display_2_out_9),
    .out_10(display_2_out_10), .out_11(display_2_out_11), .out_12(display_2_out_12),
    .out_13(display_2_out_13), .out_14(display_2_out_14), .out_15(display_2_out_14));
  coins coins_1 (.enable(EN), .reset(reset), .\output (coins_1_output));
  reward reward_1 (.jp(jackpot), .in_3(new_random_1_prize_output), .in_2(reset), .out_4(reward_1_out_4));
  DotMatrix #(.matrixcols(16), .matrixrows(16)) dotmatrix_3 (
    .col0(display_3_out_19), .col1(display_3_out_18), .col2(display_3_out_17), .col3(display_3_out_16),
    .col4(display_3_out_4), .col5(display_3_out_5), .col6(display_3_out_6), .col7(display_3_out_7),
    .col8(display_3_out_8), .col9(display_3_out_9), .col10(display_3_out_10), .col11(display_3_out_11),
    .col12(display_3_out_12), .col13(display_3_out_13), .col14(display_3_out_14), .col15(display_3_out_15));
  Display display_3 (
    .select(c), .clk(clk), .in_3(new_random_1_out_5), .out_19(display_3_out_19), .out_18(display_3_out_18),
    .out_17(display_3_out_17), .out_16(display_3_out_16), .out_4(display_3_out_4), .out_5(display_3_out_5),
    .out_6(display_3_out_6), .out_7(display_3_out_7), .out_8(display_3_out_8), .out_9(display_3_out_9),
    .out_10(display_3_out_10), .out_11(display_3_out_11), .out_12(display_3_out_12),
    .out_13(display_3_out_13), .out_14(display_3_out_14), .out_15(display_3_out_15));
  Adder adder_1 (.a(coins_1_output), .b(reward_1_out_4), .out(adder_1_out));  // open: cin, cout
  _7_Sec u_7_sec_1 (
    ._8_bits_input(adder_1_out), .out_2(n7_sec_1_out_2), .out_3(n7_sec_1_out_3), .out_4(n7_sec_1_out_4));
  Hex_Digit_Display hex_digit_display_1 (.value(n7_sec_1_out_2));  // open: dp
  Hex_Digit_Display hex_digit_display_2 (.value(n7_sec_1_out_3));  // open: dp
  Hex_Digit_Display hex_digit_display_3 (.value(n7_sec_1_out_4));  // open: dp

  // Notes on the sheet:
  //   START
  //   RESET
  //   1.นายจิรัฏฐ์ สุขพลานนท์ 6210612633
  //   2.นายปฐมพงศ์ วนาสันติพงศ์ 6210612856
  //   3.นายจิรพัฒน์ มาลีหวล 6210612765
  //   Slot Machine
  //   coins
  //   3 coins per round
  //   1. press start button.
  //    ●you can change colors whetever you want.
  //   How to play
  //   2. wait until slot stop spinning.
  //   3. if your coins= 0 press reset.
  //    ●tick enable before play (recommend frequency 32Hz or 64Hz)
  //   reward
  //    ♣ ♣ ♣ 
  //    ♦ ♦ ♦ 
  //    ♥ ♥ ♥
  //    ♠ ♠ ♠
  //   CN888.com
  //   0 coin
  //   9 coins
  //   15 coins
  //   30 coins
endmodule

module Display (
  input  select,
  input  clk,
  input  [3:0] in_3,
  output [15:0] out_4,
  output [15:0] out_5,
  output [15:0] out_6,
  output [15:0] out_7,
  output [15:0] out_8,
  output [15:0] out_9,
  output [15:0] out_10,
  output [15:0] out_11,
  output [15:0] out_12,
  output [15:0] out_13,
  output [15:0] out_14,
  output [15:0] out_15,
  output [15:0] out_16,
  output [15:0] out_17,
  output [15:0] out_18,
  output [15:0] out_19
);

  wire [15:0] multiplexer_1_out, multiplexer_2_out, multiplexer_3_out, multiplexer_4_out, multiplexer_5_out,
       multiplexer_6_out, multiplexer_7_out, multiplexer_8_out, multiplexer_9_out, multiplexer_10_out,
       multiplexer_11_out, multiplexer_12_out, multiplexer_13_out, multiplexer_14_out, multiplexer_15_out,
       multiplexer_16_out, random_1_out;

  Random #(.width(16)) random_1 (.clk(clk), .out(random_1_out));  // open: next, clr
  Multiplexer #(.select(4), .width(16)) multiplexer_1 (
    .in0({16{1'b0}}), .in1({16{1'b0}}), .in2({16{1'b0}}), .in3({16{1'b0}}), .out(multiplexer_1_out),
    .sel(in_3));  // open: in4, in5, in6, in7, in8, in9, in10, in11, in12, in13, in14, in15, en
  Multiplexer #(.select(4), .width(16)) multiplexer_2 (
    .in0({16{1'b0}}), .in1({16{1'b0}}), .in2({16{1'b0}}), .in3({16{1'b0}}), .out(multiplexer_2_out),
    .sel(in_3));  // open: in4, in5, in6, in7, in8, in9, in10, in11, in12, in13, in14, in15, en
  Multiplexer #(.select(4), .width(16)) multiplexer_3 (
    .in0(16'hf00), .in1({16{1'b0}}), .in2(16'h1c0), .in3({16{1'b0}}), .out(multiplexer_3_out), .sel(in_3));  // open: in4, in5, in6, in7, in8, in9, in10, in11, in12, in13, in14, in15, en
  Multiplexer #(.select(4), .width(16)) multiplexer_4 (
    .in0(16'h1f80), .in1({16{1'b0}}), .in2(16'h3e0), .in3(16'h1c0), .out(multiplexer_4_out), .sel(in_3));  // open: in4, in5, in6, in7, in8, in9, in10, in11, in12, in13, in14, in15, en
  Multiplexer #(.select(4), .width(16)) multiplexer_5 (
    .in0(16'h3fc0), .in1(16'h7e0), .in2(16'h3e0), .in3(16'h3e0), .out(multiplexer_5_out), .sel(in_3));  // open: in4, in5, in6, in7, in8, in9, in10, in11, in12, in13, in14, in15, en
  Multiplexer #(.select(4), .width(16)) multiplexer_6 (
    .in0(16'h3fe0), .in1(16'hff0), .in2(16'h1be4), .in3(16'h7e4), .out(multiplexer_6_out), .sel(in_3));  // open: in4, in5, in6, in7, in8, in9, in10, in11, in12, in13, in14, in15, en
  Multiplexer #(.select(4), .width(16)) multiplexer_7 (
    .in0(16'h1ff0), .in1(16'h1ff8), .in2(16'h3dcc), .in3(16'hfcc), .out(multiplexer_7_out), .sel(in_3));  // open: in4, in5, in6, in7, in8, in9, in10, in11, in12, in13, in14, in15, en
  Multiplexer #(.select(4), .width(16)) multiplexer_8 (
    .in0(16'hff8), .in1(16'h3ffc), .in2(16'h3ffc), .in3(16'h1ffc), .out(multiplexer_8_out), .sel(in_3));  // open: in4, in5, in6, in7, in8, in9, in10, in11, in12, in13, in14, in15, en
  Multiplexer #(.select(4), .width(16)) multiplexer_9 (
    .in0(16'hff8), .in1(16'h3ffc), .in2(16'h3ffc), .in3(16'h1ffc), .out(multiplexer_9_out), .sel(in_3));  // open: in4, in5, in6, in7, in8, in9, in10, in11, in12, in13, in14, in15, en
  Multiplexer #(.select(4), .width(16)) multiplexer_10 (
    .in0(16'h1ff0), .in1(16'h1ff8), .in2(16'h3dcc), .in3(16'hfcc), .out(multiplexer_10_out), .sel(in_3));  // open: in4, in5, in6, in7, in8, in9, in10, in11, in12, in13, in14, in15, en
  Multiplexer #(.select(4), .width(16)) multiplexer_11 (
    .in0(16'h3fe0), .in1(16'hff0), .in2(16'h1be4), .in3(16'h7e4), .out(multiplexer_11_out), .sel(in_3));  // open: in4, in5, in6, in7, in8, in9, in10, in11, in12, in13, in14, in15, en
  Multiplexer #(.select(4), .width(16)) multiplexer_12 (
    .in0(16'h3fc0), .in1(16'h7e0), .in2(16'h3e0), .in3(16'h3e0), .out(multiplexer_12_out), .sel(in_3));  // open: in4, in5, in6, in7, in8, in9, in10, in11, in12, in13, in14, in15, en
  Multiplexer #(.select(4), .width(16)) multiplexer_13 (
    .in0(16'h1f80), .in1({16{1'b0}}), .in2(16'h3e0), .in3(16'h1c0), .out(multiplexer_13_out), .sel(in_3));  // open: in4, in5, in6, in7, in8, in9, in10, in11, in12, in13, in14, in15, en
  Multiplexer #(.select(4), .width(16)) multiplexer_14 (
    .in0(16'hf00), .in1({16{1'b0}}), .in2(16'h1c0), .in3({16{1'b0}}), .out(multiplexer_14_out), .sel(in_3));  // open: in4, in5, in6, in7, in8, in9, in10, in11, in12, in13, in14, in15, en
  Multiplexer #(.select(4), .width(16)) multiplexer_15 (
    .in0({16{1'b0}}), .in1({16{1'b0}}), .in2({16{1'b0}}), .in3({16{1'b0}}), .out(multiplexer_15_out),
    .sel(in_3));  // open: in4, in5, in6, in7, in8, in9, in10, in11, in12, in13, in14, in15, en
  Multiplexer #(.select(4), .width(16)) multiplexer_16 (
    .in0({16{1'b0}}), .in1({16{1'b0}}), .in2({16{1'b0}}), .in3({16{1'b0}}), .out(multiplexer_16_out),
    .sel(in_3));  // open: in4, in5, in6, in7, in8, in9, in10, in11, in12, in13, in14, in15, en
  Multiplexer #(.width(16)) multiplexer_17 (
    .in0(multiplexer_1_out), .in1(random_1_out), .out(out_19), .sel(select));  // open: en
  Multiplexer #(.width(16)) multiplexer_18 (
    .in0(multiplexer_2_out), .in1(random_1_out), .out(out_18), .sel(select));  // open: en
  Multiplexer #(.width(16)) multiplexer_19 (
    .in0(multiplexer_3_out), .in1(random_1_out), .out(out_17), .sel(select));  // open: en
  Multiplexer #(.width(16)) multiplexer_20 (
    .in0(multiplexer_4_out), .in1(random_1_out), .out(out_16), .sel(select));  // open: en
  Multiplexer #(.width(16)) multiplexer_21 (
    .in0(multiplexer_5_out), .in1(random_1_out), .out(out_4), .sel(select));  // open: en
  Multiplexer #(.width(16)) multiplexer_22 (
    .in0(multiplexer_6_out), .in1(random_1_out), .out(out_5), .sel(select));  // open: en
  Multiplexer #(.width(16)) multiplexer_23 (
    .in0(multiplexer_7_out), .in1(random_1_out), .out(out_6), .sel(select));  // open: en
  Multiplexer #(.width(16)) multiplexer_24 (
    .in0(multiplexer_8_out), .in1(random_1_out), .out(out_7), .sel(select));  // open: en
  Multiplexer #(.width(16)) multiplexer_25 (
    .in0(multiplexer_9_out), .in1(random_1_out), .out(out_8), .sel(select));  // open: en
  Multiplexer #(.width(16)) multiplexer_26 (
    .in0(multiplexer_10_out), .in1(random_1_out), .out(out_9), .sel(select));  // open: en
  Multiplexer #(.width(16)) multiplexer_27 (
    .in0(multiplexer_11_out), .in1(random_1_out), .out(out_10), .sel(select));  // open: en
  Multiplexer #(.width(16)) multiplexer_28 (
    .in0(multiplexer_12_out), .in1(random_1_out), .out(out_11), .sel(select));  // open: en
  Multiplexer #(.width(16)) multiplexer_29 (
    .in0(multiplexer_13_out), .in1(random_1_out), .out(out_12), .sel(select));  // open: en
  Multiplexer #(.width(16)) multiplexer_30 (
    .in0(multiplexer_14_out), .in1(random_1_out), .out(out_13), .sel(select));  // open: en
  Multiplexer #(.width(16)) multiplexer_31 (
    .in0(multiplexer_15_out), .in1(random_1_out), .out(out_14), .sel(select));  // open: en
  Multiplexer #(.width(16)) multiplexer_32 (
    .in0(multiplexer_16_out), .in1(random_1_out), .out(out_15), .sel(select));  // open: en
endmodule

module _7_Sec (
  input  [7:0] _8_bits_input,
  output [3:0] out_2,
  output [3:0] out_3,
  output [3:0] out_4
);

  ROM #(.dataWidth(12)) rom_1 (.addr(_8_bits_input), .data({out_2, out_3, out_4}));  // open: sel

  // Notes on the sheet:
  //   contents of rom_1 (hex, n*v repeats v):
  //   0 1 2 3 4 5 6 7 8 9 10 11 12 13 14 15 16 17 18 19 20 21 22 23 24 25 26 27 28 29 30 31 32 33 34 35 36
  //   37 38 39 40 41 42 43 44 45 46 47 48 49 50 51 52 53 54 55 56 57 58 59 60 61 62 63 64 65 66 67 68 69
  //   70 71 72 73 74 75 76 77 78 79 80 81 82 83 84 85 86 87 88 89 90 91 92 93 94 95 96 97 98 99 100 101
  //   102 103 104 105 106 107 108 109 110 111 112 113 114 115 116 117 118 119 120 121 122 123 124 125 126
  //   127 128 129 130 131 132 133 134 135 136 137 138 139 140 141 142 143 144 145 146 147 148 149 150 151
  //   152 153 154 155 156 157 158 159 160 161 162 163 164 165 166 167 168 169 170 171 172 173 174 175 176
  //   177 178 179 180 181 182 183 184 185 186 187 188 189 190 191 192 193 194 195 196 197 198 199 200 201
  //   202 203 204 205 206 207 208 209 210 211 212 213 214 215 216 217 218 219 220 221 222 223 224 225 226
  //   227 228 229 230 231 232 233 234 235 236 237 238 239 240 241 242 243 244 245 246 247 248 249 250 251
  //   252 253 254 255
endmodule

module random (
  input  clock,
  input  button,
  output [3:0] out_3,
  output [3:0] out_4,
  output [3:0] out_5,
  output Select
);

  wire and_1_out, and_2_out, not_1_out;
  wire [2:0] random_1_out, random_2_out, random_3_out, register_1_q, register_2_q, register_3_q;

  and and_1 (and_1_out, 1'b1, clock);
  Random #(.width(3), .seed(4154151)) random_1 (.clk(and_1_out), .out(random_1_out));  // open: next, clr
  Random #(.width(3), .seed(41515145)) random_2 (.clk(clock), .out(random_2_out));  // open: next, clr
  and and_2 (and_2_out, and_1_out, clock);
  Random #(.width(3), .seed(154854)) random_3 (.clk(and_2_out), .out(random_3_out));  // open: next, clr
  Shift_Register #(.length(16)) shift_register_1 (
    .in(1'b0), .clk(clock), .load(button), .d0(1'b1), .d1(1'b1), .d2(1'b1), .d3(1'b1), .d4(1'b1), .d5(1'b1),
    .d6(1'b1), .d7(1'b1), .d8(1'b1), .d9(1'b1), .d10(1'b1), .d11(1'b1), .d12(1'b1), .d13(1'b1), .d14(1'b1),
    .d15(1'b1), .q15(Select));  // open: shift, out, clr, q0, q1, q2, q3, q4, q5, q6, q7, q8, q9, q10, q11, q12, q13, q14
  Register #(.width(3)) register_1 (.D(random_1_out), .Q(register_1_q), .clk(not_1_out));  // open: en, clr
  Register #(.width(3)) register_2 (.D(random_2_out), .Q(register_2_q), .clk(not_1_out));  // open: en, clr
  Register #(.width(3)) register_3 (.D(random_3_out), .Q(register_3_q), .clk(not_1_out));  // open: en, clr
  not not_1 (not_1_out, Select);
  Multiplexer #(.select(3), .width(4), .enable("false")) multiplexer_1 (
    .in0(4'b0000), .in1(4'b0000), .in2(4'b0001), .in3(4'b0001), .in4(4'b0010), .in5(4'b0010), .in6(4'b0011),
    .in7(4'b0011), .out(out_3), .sel(register_1_q));
  Multiplexer #(.select(3), .width(4), .enable("false")) multiplexer_2 (
    .in0(4'b0000), .in1(4'b0000), .in2(4'b0001), .in3(4'b0001), .in4(4'b0010), .in5(4'b0010), .in6(4'b0011),
    .in7(4'b0011), .out(out_4), .sel(register_2_q));
  Multiplexer #(.select(3), .width(4), .enable("false")) multiplexer_3 (
    .in0(4'b0000), .in1(4'b0000), .in2(4'b0001), .in3(4'b0001), .in4(4'b0010), .in5(4'b0010), .in6(4'b0011),
    .in7(4'b0011), .out(out_5), .sel(register_3_q));

  // Other names for the same wires on the sheet: timer = Select
endmodule

module new_Random (
  input  clock,
  input  button,
  output [3:0] out_3,
  output [3:0] out_4,
  output [3:0] out_5,
  output Check_win,
  output [1:0] Prize_output,
  output Select1,
  output Select2,
  output Select3
);

  wire and_1_out, and_2_out, and_3_out, and_4_out, and_6_out, comparator_1_eq, comparator_2_eq, not_1_out,
       not_2_out, not_3_out, not_4_out, not_5_out, not_6_out, shift_register_1_q16, shift_register_1_q17,
       shift_register_1_q18, shift_register_1_q19, shift_register_1_q20, shift_register_1_q21,
       shift_register_1_q22, shift_register_1_q23, shift_register_1_q24, shift_register_1_q25,
       shift_register_1_q26, shift_register_1_q27, shift_register_1_q28, shift_register_1_q29,
       shift_register_1_q30, shift_register_1_q31, shift_register_2_q16, shift_register_2_q17,
       shift_register_2_q18, shift_register_2_q19, shift_register_2_q20, shift_register_2_q21,
       shift_register_2_q22, shift_register_2_q23, shift_register_2_q24, shift_register_2_q25,
       shift_register_2_q26, shift_register_2_q27, shift_register_2_q28, shift_register_2_q29,
       shift_register_2_q30, shift_register_2_q31, shift_register_3_q16, shift_register_3_q17,
       shift_register_3_q18, shift_register_3_q19, shift_register_3_q20, shift_register_3_q21,
       shift_register_3_q22, shift_register_3_q23, shift_register_3_q24, shift_register_3_q25,
       shift_register_3_q26, shift_register_3_q27, shift_register_3_q28, shift_register_3_q29,
       shift_register_3_q30, shift_register_3_q31, shift_register_4_out, Timer4;
  wire [2:0] random_1_out, random_2_out, random_3_out, register_1_q, register_2_q, register_3_q;
  wire [15:0] random_4_out, random_5_out, random_6_out;

  and and_1 (and_1_out, clock, 1'b1);
  and and_2 (and_2_out, clock, and_1_out);
  Random #(.width(3), .seed(1231231)) random_1 (.clk(clock), .out(random_1_out));  // open: next, clr
  Random #(.width(3), .seed(326125)) random_2 (.clk(and_1_out), .out(random_2_out));  // open: next, clr
  Random #(.width(3), .seed(97643743)) random_3 (.clk(and_2_out), .out(random_3_out));  // open: next, clr
  and and_3 (and_3_out, clock, clock);
  not not_1 (not_1_out, clock);
  and and_4 (and_4_out, not_1_out, not_2_out);
  not not_2 (not_2_out, clock);
  Random #(.width(16), .seed(97643743)) random_4 (.clk(clock), .out(random_4_out));  // open: next, clr
  Shift_Register #(.length(32)) shift_register_1 (
    .in(1'b0), .clk(clock), .load(button), .d0(random_4_out[15]), .d1(random_4_out[14]),
    .d2(random_4_out[13]), .d3(random_4_out[12]), .d4(random_4_out[11]), .d5(random_4_out[10]),
    .d6(random_4_out[9]), .d7(random_4_out[8]), .d8(random_4_out[7]), .d9(random_4_out[6]),
    .d10(random_4_out[5]), .d11(random_4_out[4]), .d12(random_4_out[3]), .d13(random_4_out[2]),
    .d14(random_4_out[1]), .d15(random_4_out[0]), .d16(1'b1), .q16(shift_register_1_q16), .d17(1'b1),
    .q17(shift_register_1_q17), .d18(1'b1), .q18(shift_register_1_q18), .d19(1'b1),
    .q19(shift_register_1_q19), .d20(1'b1), .q20(shift_register_1_q20), .d21(1'b1),
    .q21(shift_register_1_q21), .d22(1'b1), .q22(shift_register_1_q22), .d23(1'b1),
    .q23(shift_register_1_q23), .d24(1'b1), .q24(shift_register_1_q24), .d25(1'b1),
    .q25(shift_register_1_q25), .d26(1'b1), .q26(shift_register_1_q26), .d27(1'b1),
    .q27(shift_register_1_q27), .d28(1'b1), .q28(shift_register_1_q28), .d29(1'b1),
    .q29(shift_register_1_q29), .d30(1'b1), .q30(shift_register_1_q30), .d31(1'b1), .q31(shift_register_1_q31));  // open: shift, out, clr, q0, q1, q2, q3, q4, q5, q6, q7, q8, q9, q10, q11, q12, q13, q14, q15
  Random #(.width(16), .seed(263265)) random_5 (.clk(and_3_out), .out(random_5_out));  // open: next, clr
  Shift_Register #(.length(32)) shift_register_2 (
    .in(1'b0), .clk(clock), .load(button), .d0(random_5_out[15]), .d1(random_5_out[14]),
    .d2(random_5_out[13]), .d3(random_5_out[12]), .d4(random_5_out[11]), .d5(random_5_out[10]),
    .d6(random_5_out[9]), .d7(random_5_out[8]), .d8(random_5_out[7]), .d9(random_5_out[6]),
    .d10(random_5_out[5]), .d11(random_5_out[4]), .d12(random_5_out[3]), .d13(random_5_out[2]),
    .d14(random_5_out[1]), .d15(random_5_out[0]), .d16(1'b1), .q16(shift_register_2_q16), .d17(1'b1),
    .q17(shift_register_2_q17), .d18(1'b1), .q18(shift_register_2_q18), .d19(1'b1),
    .q19(shift_register_2_q19), .d20(1'b1), .q20(shift_register_2_q20), .d21(1'b1),
    .q21(shift_register_2_q21), .d22(1'b1), .q22(shift_register_2_q22), .d23(1'b1),
    .q23(shift_register_2_q23), .d24(1'b1), .q24(shift_register_2_q24), .d25(1'b1),
    .q25(shift_register_2_q25), .d26(1'b1), .q26(shift_register_2_q26), .d27(1'b1),
    .q27(shift_register_2_q27), .d28(1'b1), .q28(shift_register_2_q28), .d29(1'b1),
    .q29(shift_register_2_q29), .d30(1'b1), .q30(shift_register_2_q30), .d31(1'b1), .q31(shift_register_2_q31));  // open: shift, out, clr, q0, q1, q2, q3, q4, q5, q6, q7, q8, q9, q10, q11, q12, q13, q14, q15
  Random #(.width(16), .seed(2147236)) random_6 (.clk(and_4_out), .out(random_6_out));  // open: next, clr
  Shift_Register #(.length(32)) shift_register_3 (
    .in(1'b0), .clk(clock), .load(button), .d0(random_6_out[15]), .d1(random_6_out[14]),
    .d2(random_6_out[13]), .d3(random_6_out[12]), .d4(random_6_out[11]), .d5(random_6_out[10]),
    .d6(random_6_out[9]), .d7(random_6_out[8]), .d8(random_6_out[7]), .d9(random_6_out[6]),
    .d10(random_6_out[5]), .d11(random_6_out[4]), .d12(random_6_out[3]), .d13(random_6_out[2]),
    .d14(random_6_out[1]), .d15(random_6_out[0]), .d16(1'b1), .q16(shift_register_3_q16), .d17(1'b1),
    .q17(shift_register_3_q17), .d18(1'b1), .q18(shift_register_3_q18), .d19(1'b1),
    .q19(shift_register_3_q19), .d20(1'b1), .q20(shift_register_3_q20), .d21(1'b1),
    .q21(shift_register_3_q21), .d22(1'b1), .q22(shift_register_3_q22), .d23(1'b1),
    .q23(shift_register_3_q23), .d24(1'b1), .q24(shift_register_3_q24), .d25(1'b1),
    .q25(shift_register_3_q25), .d26(1'b1), .q26(shift_register_3_q26), .d27(1'b1),
    .q27(shift_register_3_q27), .d28(1'b1), .q28(shift_register_3_q28), .d29(1'b1),
    .q29(shift_register_3_q29), .d30(1'b1), .q30(shift_register_3_q30), .d31(1'b1), .q31(shift_register_3_q31));  // open: shift, out, clr, q0, q1, q2, q3, q4, q5, q6, q7, q8, q9, q10, q11, q12, q13, q14, q15
  Shift_Register #(.length(32)) shift_register_4 (
    .in(1'b0), .clk(clock), .out(shift_register_4_out), .load(button), .d0(1'b1), .d1(1'b1), .d2(1'b1),
    .d3(1'b1), .d4(1'b1), .d5(1'b1), .d6(1'b1), .d7(1'b1), .d8(1'b1), .d9(1'b1), .d10(1'b1), .d11(1'b1),
    .d12(1'b1), .d13(1'b1), .d14(1'b1), .d15(1'b1), .d16(1'b1), .d17(1'b1), .d18(1'b1), .d19(1'b1),
    .d20(1'b1), .d21(1'b1), .d22(1'b1), .d23(1'b1), .d24(1'b1), .d25(1'b1), .d26(1'b1), .d27(1'b1),
    .d28(1'b1), .d29(1'b1), .d30(1'b1), .d31(1'b1));  // open: shift, clr, q0, q1, q2, q3, q4, q5, q6, q7, q8, q9, q10, q11, q12, q13, q14, q15, q16, q17, q18, q19, q20, q21, q22, q23, q24, q25, q26, q27, q28, q29, q30, q31
  Register #(.width(3)) register_1 (.D(random_1_out), .Q(register_1_q), .clk(not_3_out));  // open: en, clr
  not not_3 (not_3_out, Select1);
  Register #(.width(3)) register_2 (.D(random_2_out), .Q(register_2_q), .clk(not_4_out));  // open: en, clr
  not not_4 (not_4_out, Select2);
  Register #(.width(3)) register_3 (.D(random_3_out), .Q(register_3_q), .clk(not_5_out));  // open: en, clr
  not not_5 (not_5_out, Select3);
  Multiplexer #(.select(3), .width(4), .enable("false")) multiplexer_1 (
    .in0(4'b0000), .in1(4'b0000), .in2(4'b0001), .in3(4'b0001), .in4(4'b0010), .in5(4'b0010), .in6(4'b0011),
    .in7(4'b0011), .out(out_3), .sel(register_1_q));
  Multiplexer #(.select(3), .width(4), .enable("false")) multiplexer_2 (
    .in0(4'b0000), .in1(4'b0000), .in2(4'b0001), .in3(4'b0001), .in4(4'b0010), .in5(4'b0010), .in6(4'b0011),
    .in7(4'b0011), .out(out_4), .sel(register_2_q));
  bus_timer bus_timer_1 (
    .out_17(Select1), .in_9(shift_register_1_q16), .in_10(shift_register_1_q17),
    .in_11(shift_register_1_q18), .in_12(shift_register_1_q19), .in_13(shift_register_1_q20),
    .in_14(shift_register_1_q21), .in_15(shift_register_1_q22), .in_16(shift_register_1_q23),
    .in_1(shift_register_1_q24), .in_2(shift_register_1_q25), .in_3(shift_register_1_q26),
    .in_4(shift_register_1_q27), .in_5(shift_register_1_q28), .in_6(shift_register_1_q29),
    .in_7(shift_register_1_q30), .in_8(shift_register_1_q31));
  bus_timer bus_timer_2 (
    .out_17(Select2), .in_9(shift_register_2_q16), .in_10(shift_register_2_q17),
    .in_11(shift_register_2_q18), .in_12(shift_register_2_q19), .in_13(shift_register_2_q20),
    .in_14(shift_register_2_q21), .in_15(shift_register_2_q22), .in_16(shift_register_2_q23),
    .in_1(shift_register_2_q24), .in_2(shift_register_2_q25), .in_3(shift_register_2_q26),
    .in_4(shift_register_2_q27), .in_5(shift_register_2_q28), .in_6(shift_register_2_q29),
    .in_7(shift_register_2_q30), .in_8(shift_register_2_q31));
  bus_timer bus_timer_3 (
    .out_17(Select3), .in_9(shift_register_3_q16), .in_10(shift_register_3_q17),
    .in_11(shift_register_3_q18), .in_12(shift_register_3_q19), .in_13(shift_register_3_q20),
    .in_14(shift_register_3_q21), .in_15(shift_register_3_q22), .in_16(shift_register_3_q23),
    .in_1(shift_register_3_q24), .in_2(shift_register_3_q25), .in_3(shift_register_3_q26),
    .in_4(shift_register_3_q27), .in_5(shift_register_3_q28), .in_6(shift_register_3_q29),
    .in_7(shift_register_3_q30), .in_8(shift_register_3_q31));
  Multiplexer #(.select(3), .width(4), .enable("false")) multiplexer_3 (
    .in0(4'b0000), .in1(4'b0000), .in2(4'b0001), .in3(4'b0001), .in4(4'b0010), .in5(4'b0010), .in6(4'b0011),
    .in7(4'b0011), .out(out_5), .sel(register_3_q));
  Shift_Register shift_register_5 (
    .in(shift_register_4_out), .clk(clock), .load(button), .d0(1'b1), .d1(1'b1), .d2(1'b1), .d3(1'b1),
    .d4(1'b1), .d5(1'b1), .d6(1'b1), .d7(1'b1), .q7(Timer4));  // open: shift, out, clr, q0, q1, q2, q3, q4, q5, q6
  Comparator #(.width(4)) comparator_1 (.a(out_5), .b(out_4), .eq(comparator_1_eq));  // open: gt, lt
  Comparator #(.width(4)) comparator_2 (.a(out_4), .b(out_3), .eq(comparator_2_eq));  // open: gt, lt
  not not_6 (not_6_out, Timer4);
  and and_5 (Check_win, not_6_out, and_6_out);
  and and_6 (and_6_out, comparator_1_eq, comparator_2_eq);
  Multiplexer #(.select(2), .width(2), .enable("false")) multiplexer_4 (
    .in0(2'b10), .in1(2'b01), .in2(2'b00), .in3(2'b11), .out(Prize_output), .sel(out_3[1:0]));

  // Other names for the same wires on the sheet: output1[3:0] = out_3; clk = clock; output2[3:0] = out_4;
  //   output3[3:0] = out_5; Timer1 = Select1; Timer2 = Select2; Timer3 = Select3
endmodule

module bus_timer (
  input  in_1,
  input  in_2,
  input  in_3,
  input  in_4,
  input  in_5,
  input  in_6,
  input  in_7,
  input  in_8,
  input  in_9,
  input  in_10,
  input  in_11,
  input  in_12,
  input  in_13,
  input  in_14,
  input  in_15,
  input  in_16,
  output out_17
);

  wire or_1_out, or_2_out;

  or or_1 (or_1_out, in_16, in_15, in_14, in_13, in_12, in_11, in_10, in_9);
  or or_2 (or_2_out, in_8, in_7, in_6, in_5, in_4, in_3, in_2, in_1);
  or or_3 (out_17, or_1_out, or_2_out);
endmodule

module coins (
  input  enable,
  input  reset,
  output [7:0] \output 
);

  wire rom_1_data;
  wire [1:0] counter_1_q;
  wire [7:0] multiplexer_1_out, or_1_out, rom_2_data, subtractor_1_out;

  Multiplexer #(.width(8), .enable("false")) multiplexer_1 (
    .in0(8'h1e), .in1({8{1'b0}}), .out(multiplexer_1_out), .sel(rom_1_data));
  assign or_1_out = multiplexer_1_out | subtractor_1_out;  // OR_Gate or_1, 8 bits wide
  Register register_1 (.D(or_1_out), .Q(\output ), .clk(enable), .clr(reset));  // open: en
  Counter #(.width(2), .max('h1), .ongoal("stay")) counter_1 (
    .Q(counter_1_q), .clk(enable), .clr(reset));  // open: load, D, count, carry
  ROM #(.addrWidth(2), .dataWidth(1)) rom_1 (.addr(counter_1_q), .data(rom_1_data));  // open: sel
  Subtractor subtractor_1 (.a(\output ), .b(rom_2_data), .out(subtractor_1_out));  // open: bin, bout
  ROM #(.addrWidth(2)) rom_2 (.addr(counter_1_q), .data(rom_2_data));  // open: sel

  // Notes on the sheet:
  //   contents of rom_1 (hex, n*v repeats v):
  //   0 1
  //   contents of rom_2 (hex, n*v repeats v):
  //   0 3
endmodule

module reward (
  input  jp,
  input  in_2,
  input  [1:0] in_3,
  output [7:0] out_4
);

  wire [7:0] adder_1_out, multiplexer_1_out;

  Multiplexer #(.select(2), .width(8), .enable("false")) multiplexer_1 (
    .in0({8{1'b0}}), .in1(8'h9), .in2(8'hf), .in3(8'h1e), .out(multiplexer_1_out), .sel(in_3));
  Adder adder_1 (.a(out_4), .b(multiplexer_1_out), .out(adder_1_out));  // open: cin, cout
  Register register_1 (.D(adder_1_out), .Q(out_4), .clk(jp), .clr(in_2));  // open: en
endmodule
